# Fritzing sketch PanasonicIrRemote (saved by Fritzing 0.9.3b)
breadboards: 1

parts:
  パーツ1 = Arduino Uno (Rev3)
  D1 = LTE-302 [package=lte-302]
  R1 = Resistor [tolerance=±5% resistance=150 package=THT]

nets:
  N1: パーツ1.GND, D1.C
  N2: パーツ1.D3_PWM, R1.Pin_1
  N3: D1.A, R1.Pin_0
